# Fritzing sketch fritzing (saved by Fritzing 0.9.10b)

parts:
  Mod1 = Raspberry Pi 4B
  PWM1 = PCA9685 16x12-bit PWM Breakout
  J1 = Basic Servo

nets:
  N1: Mod1.3V3, PWM1.no_name_yet#505
  N2: Mod1.GPIO2, PWM1.no_name_yet#504
  N3: Mod1.GPIO3, PWM1.no_name_yet#503
  GND: Mod1.GND, PWM1.no_name_yet#501, PWM1.no_name_yet#701, PWM1.no_name_yet#1000, J1.gnd
  N4: PWM1.no_name_yet#0, J1.pulse
  N5: PWM1.no_name_yet#100, PWM1.no_name_yet#706, J1.vcc
